// Logisim project alu.circ as structural Verilog: 19 circuits, main circuit main
module main (
  input  Load,
  input  [3:0] A_Input,
  input  [3:0] B_Input,
  input  On,
  input  [3:0] Operation,
  output Maximum_Count_Reached,
  output [3:0] Output,
  output C,
  output N,
  output Z,
  output V
);

  wire and_1_out, and_2_out, and_3_out, Clock_out, d_ff_1_q, n4_bit_decrementer_1_carry_out,
       n4_bit_full_adder_1_carry_out, n4_bit_increment_1_carry_out, n4_bit_subtractor_1_overflow___underflow,
       not_1_out, not_2_out, not_3_out, not_4_out, or_1_out, or_3_out, t_ff_1_q, xor_1_out;
  wire [3:0] A_q, B_q, controlled_buffer_1_out, n4_bit_and_1_output, n4_bit_decrementer_1_output,
       n4_bit_full_adder_1_output, n4_bit_increment_1_output, n4_bit_left_rotate_1_output,
       n4_bit_left_shift_1_output, n4_bit_or_1_output, n4_bit_right_rotate_1_output,
       n4_bit_right_shift_1_output, n4_bit_subtractor_1_output, n4_bit_xor_1_output, register_1_q;

  Clock Clock (.out(Clock_out));
  and and_1 (and_1_out, Clock_out, t_ff_1_q);
  Counter #(.width(4), .max('h3)) counter_1 (
    .carry(Maximum_Count_Reached), .clk(and_1_out), .clr(d_ff_1_q));  // open: load, D, count, Q
  T_Flip_Flop t_ff_1 (
    .clk(Clock_out), .T(1'b1), .Q(t_ff_1_q), .reset(Maximum_Count_Reached), .en(On));  // open: Qn, preset
  assign controlled_buffer_1_out = Load ? A_Input : 4'bz;  // Controlled_Buffer controlled_buffer_1
  D_Flip_Flop d_ff_1 (.clk(Clock_out), .D(Maximum_Count_Reached), .Q(d_ff_1_q), .en(1'b1));  // open: Qn, preset, reset
  or or_1 (or_1_out, Load, Maximum_Count_Reached);
  assign controlled_buffer_1_out = not_1_out ? register_1_q : 4'bz;  // Controlled_Buffer controlled_buffer_2
  not not_1 (not_1_out, Load);
  Register #(.width(4)) A (.D(controlled_buffer_1_out), .en(or_1_out), .Q(A_q), .clk(Clock_out));  // open: clr
  Register #(.width(4)) B (.D(B_Input), .Q(B_q), .clk(Clock_out));  // open: en, clr
  _4_bit_xor u_4_bit_xor_1 (.A_In(A_q), .B_In(B_q), .Output(n4_bit_xor_1_output));
  _4_bit_or u_4_bit_or_1 (.A_In(A_q), .B_In(B_q), .Output(n4_bit_or_1_output));
  _4_bit_and u_4_bit_and_1 (.A_In(A_q), .B_In(B_q), .Output(n4_bit_and_1_output));
  _4_bit_right_rotate u_4_bit_right_rotate_1 (.Input(A_q), .Output(n4_bit_right_rotate_1_output));
  _4_bit_left_rotate u_4_bit_left_rotate_1 (.Input(A_q), .Output(n4_bit_left_rotate_1_output));
  _16_to_4_multiplexer u_16_to_4_multiplexer_1 (
    .Operation(Operation), .Operation_2({N, Output[2:0]}), .Data_16(n4_bit_full_adder_1_output),
    .Data_15(n4_bit_subtractor_1_output), .Data_14(n4_bit_increment_1_output),
    .Data_13(n4_bit_decrementer_1_output), .Data_9(n4_bit_right_rotate_1_output),
    .Data_10(n4_bit_left_rotate_1_output), .Data_11(n4_bit_right_shift_1_output),
    .Data_12(n4_bit_left_shift_1_output), .Data_6(n4_bit_xor_1_output), .Data_7(n4_bit_or_1_output),
    .Data_8(n4_bit_and_1_output));  // open: Data_5, Data, Data_2, Data_3, Data_4
  _4_bit_right_shift u_4_bit_right_shift_1 (.Input(A_q), .Output(n4_bit_right_shift_1_output));
  _4_bit_left_shift u_4_bit_left_shift_1 (.Input(A_q), .Output(n4_bit_left_shift_1_output));
  Register #(.width(4)) register_1 (.D({N, Output[2:0]}), .Q(register_1_q), .clk(Clock_out));  // open: en, clr
  _4_bit_decrementer u_4_bit_decrementer_1 (
    .Input(A_q), .Output(n4_bit_decrementer_1_output), .Carry_Out(n4_bit_decrementer_1_carry_out));
  _4_bit_increment u_4_bit_increment_1 (
    .Input(A_q), .Carry_Out(n4_bit_increment_1_carry_out), .Output(n4_bit_increment_1_output));
  _4_to_for_multiplexer u_4_to_for_multiplexer_1 (
    .Operation(Operation), .Data(n4_bit_decrementer_1_carry_out), .Data_2(n4_bit_increment_1_carry_out),
    .Data_3(n4_bit_subtractor_1_overflow___underflow), .Data_4(n4_bit_full_adder_1_carry_out), .Operation_2(C));
  xor xor_1 (xor_1_out, A_q[3], 1'b0);
  and and_2 (and_2_out, xor_1_out, A_q[3], not_2_out);
  _4_bit_subtractor u_4_bit_subtractor_1 (
    .B_In(B_q), .A_In(A_q), .Output(n4_bit_subtractor_1_output),
    .Overflow___Underflow(n4_bit_subtractor_1_overflow___underflow), .in_3(1'b1));
  not not_2 (not_2_out, N);
  not not_3 (not_3_out, xor_1_out);
  or or_2 (V, and_2_out, and_3_out);
  not not_4 (not_4_out, A_q[3]);
  and and_3 (and_3_out, not_3_out, not_4_out, N);
  _4_bit_full_adder u_4_bit_full_adder_1 (
    .A_In(A_q), .B_In(B_q), .Output(n4_bit_full_adder_1_output), .Carry_Out(n4_bit_full_adder_1_carry_out),
    .Carry_In(1'b0));
  or or_3 (or_3_out, N, Output[2], Output[1], Output[0]);
  not not_5 (Z, or_3_out);

  assign Output[3] = N;

  // Notes on the sheet:
  //   1- Introducir A
  //   2- Introducir B
  //   3- Introducir Address (Operation)
  //   5- Poner On a 1 para comenzar a funcionar
  //   4- Poner Load a 1 para habilitar el paso de A al acumulador
  //   6- Primera subida de reloj para cargar registros A y B (devolver a 0 antes del siguiente ciclo)
  //   8- Poner On a 0 para evitar que el toggle cambie
  //   7- Poner, si no lo está ya, Load a 0 para habilitar el paso de la Salida al acumulador
  //   9- Dar ciclos de reloj hasta que se haya actualizado el acumulador (devolver a 0 antes del siguiente ciclo)
  //   10- Ir a paso 1 para operar con un nuevo valor de A o al 3 para continuar operando con lo que hay en el acumulador
  //   Si dejo On encendido, puedo operar constantemente con lo que hay en el acumulador. Y si en algún momento enciando y apago Load lo que hago es resetear el registro A a un nuevo valor y a partir de ahí, operar otra vez continuamente con el acumulador.
endmodule

// 1-bit Half\nAdder
module _1_bit_half_adder (
  input  A_In,
  input  B_In,
  output Sum_Out,
  output Carry_Out
);

  xor xor_1 (Sum_Out, A_In, B_In);
  and and_1 (Carry_Out, A_In, B_In);
endmodule

// 4-Bit\nFull Adder
module _4_bit_full_adder (
  input  [3:0] A_In,
  input  [3:0] B_In,
  input  Carry_In,
  output Carry_Out,
  output [3:0] Output
);

  wire n1_bit_full_adder_2_carry_out, n1_bit_full_adder_3_carry_out, n1_bit_full_adder_4_carry_out;

  _1_bit_full_adder u_1_bit_full_adder_1 (
    .Carry_In(n1_bit_full_adder_2_carry_out), .A_In(A_In[3]), .B_In(B_In[3]), .Sum_Out(Output[3]),
    .Carry_Out(Carry_Out));
  _1_bit_full_adder u_1_bit_full_adder_2 (
    .Carry_In(n1_bit_full_adder_3_carry_out), .A_In(A_In[2]), .B_In(B_In[2]), .Sum_Out(Output[2]),
    .Carry_Out(n1_bit_full_adder_2_carry_out));
  _1_bit_full_adder u_1_bit_full_adder_3 (
    .Carry_In(n1_bit_full_adder_4_carry_out), .A_In(A_In[1]), .B_In(B_In[1]), .Sum_Out(Output[1]),
    .Carry_Out(n1_bit_full_adder_3_carry_out));
  _1_bit_full_adder u_1_bit_full_adder_4 (
    .Carry_In(Carry_In), .A_In(A_In[0]), .B_In(B_In[0]), .Sum_Out(Output[0]),
    .Carry_Out(n1_bit_full_adder_4_carry_out));
endmodule

// 1-Bit Full\nAdder
module _1_bit_full_adder (
  input  Carry_In,
  input  A_In,
  input  B_In,
  output Sum_Out,
  output Carry_Out
);

  wire n1_bit_half_adder_1_carry_out, n1_bit_half_adder_1_sum_out, n1_bit_half_adder_2_carry_out;

  _1_bit_half_adder u_1_bit_half_adder_1 (
    .A_In(A_In), .B_In(B_In), .Sum_Out(n1_bit_half_adder_1_sum_out), .Carry_Out(n1_bit_half_adder_1_carry_out));
  _1_bit_half_adder u_1_bit_half_adder_2 (
    .A_In(Carry_In), .B_In(n1_bit_half_adder_1_sum_out), .Sum_Out(Sum_Out),
    .Carry_Out(n1_bit_half_adder_2_carry_out));
  or or_1 (Carry_Out, n1_bit_half_adder_2_carry_out, n1_bit_half_adder_1_carry_out);
endmodule

// 4-Bit\nIncrementer
module _4_bit_increment (
  input  [3:0] Input,
  output Carry_Out,
  output [3:0] Output
);

  wire n1_bit_half_adder_2_carry_out, n1_bit_half_adder_3_carry_out, n1_bit_half_adder_4_carry_out;

  _1_bit_half_adder u_1_bit_half_adder_1 (
    .A_In(n1_bit_half_adder_2_carry_out), .B_In(Input[3]), .Sum_Out(Output[3]), .Carry_Out(Carry_Out));
  _1_bit_half_adder u_1_bit_half_adder_2 (
    .A_In(n1_bit_half_adder_3_carry_out), .B_In(Input[2]), .Sum_Out(Output[2]),
    .Carry_Out(n1_bit_half_adder_2_carry_out));
  _1_bit_half_adder u_1_bit_half_adder_3 (
    .A_In(n1_bit_half_adder_4_carry_out), .B_In(Input[1]), .Sum_Out(Output[1]),
    .Carry_Out(n1_bit_half_adder_3_carry_out));
  _1_bit_half_adder u_1_bit_half_adder_4 (
    .A_In(1'b1), .B_In(Input[0]), .Sum_Out(Output[0]), .Carry_Out(n1_bit_half_adder_4_carry_out));
endmodule

// 4-Bit\nDecrementer
module _4_bit_decrementer (
  input  [3:0] Input,
  output Carry_Out,
  output [3:0] Output
);

  wire n1_bit_full_adder_2_carry_out, n1_bit_full_adder_3_carry_out, n1_bit_full_adder_4_carry_out;

  _1_bit_full_adder u_1_bit_full_adder_1 (
    .Carry_In(n1_bit_full_adder_2_carry_out), .A_In(Input[3]), .B_In(1'b1), .Sum_Out(Output[3]),
    .Carry_Out(Carry_Out));
  _1_bit_full_adder u_1_bit_full_adder_2 (
    .Carry_In(n1_bit_full_adder_3_carry_out), .A_In(Input[2]), .B_In(1'b1), .Sum_Out(Output[2]),
    .Carry_Out(n1_bit_full_adder_2_carry_out));
  _1_bit_full_adder u_1_bit_full_adder_3 (
    .Carry_In(n1_bit_full_adder_4_carry_out), .A_In(Input[1]), .B_In(1'b1), .Sum_Out(Output[1]),
    .Carry_Out(n1_bit_full_adder_3_carry_out));
  _1_bit_full_adder u_1_bit_full_adder_4 (
    .Carry_In(1'b0), .A_In(Input[0]), .B_In(1'b1), .Sum_Out(Output[0]),
    .Carry_Out(n1_bit_full_adder_4_carry_out));
endmodule

// 4-Bit\nAND
module _4_bit_and (
  input  [3:0] A_In,
  input  [3:0] B_In,
  output [3:0] Output
);

  and and_1 (Output[3], A_In[3], B_In[3]);
  and and_2 (Output[2], A_In[2], B_In[2]);
  and and_3 (Output[1], A_In[1], B_In[1]);
  and and_4 (Output[0], A_In[0], B_In[0]);
endmodule

// 4-Bit\nOR
module _4_bit_or (
  input  [3:0] A_In,
  input  [3:0] B_In,
  output [3:0] Output
);

  or or_1 (Output[3], A_In[3], B_In[3]);
  or or_2 (Output[2], A_In[2], B_In[2]);
  or or_3 (Output[1], A_In[1], B_In[1]);
  or or_4 (Output[0], A_In[0], B_In[0]);
endmodule

// 4-Bit\nXOR
module _4_bit_xor (
  input  [3:0] A_In,
  input  [3:0] B_In,
  output [3:0] Output
);

  xor xor_1 (Output[3], A_In[3], B_In[3]);
  xor xor_2 (Output[2], A_In[2], B_In[2]);
  xor xor_3 (Output[1], A_In[1], B_In[1]);
  xor xor_4 (Output[0], A_In[0], B_In[0]);
endmodule

// 4-Bit One's\nComplement
module _4_bit_ones_complement (
  input  [3:0] Input,
  output [3:0] Output
);

  not not_1 (Output[3], Input[3]);
  not not_2 (Output[2], Input[2]);
  not not_3 (Output[1], Input[1]);
  not not_4 (Output[0], Input[0]);
endmodule

// 4-Bit\nSubtractor
module _4_bit_subtractor (
  input  [3:0] B_In,
  input  [3:0] A_In,
  input  in_3,
  output Overflow___Underflow,
  output [3:0] Output
);

  wire n4_bit_full_adder_1_carry_out;
  wire [3:0] n4_bit_ones_complement_1_output;

  xor xor_1 (Overflow___Underflow, n4_bit_full_adder_1_carry_out, in_3);
  _4_bit_ones_complement u_4_bit_ones_complement_1 (.Input(B_In), .Output(n4_bit_ones_complement_1_output));
  _4_bit_full_adder u_4_bit_full_adder_1 (
    .A_In(A_In), .B_In(n4_bit_ones_complement_1_output), .Output(Output),
    .Carry_Out(n4_bit_full_adder_1_carry_out), .Carry_In(in_3));
endmodule

// 4-to-16 Decoder
module _4_to_16_decoder (
  input  Data_In,
  input  [3:0] Address__operation,
  output [15:0] out_3
);

  wire not_1_out, not_2_out, not_3_out, not_4_out;

  not not_1 (not_1_out, Address__operation[0]);
  not not_2 (not_2_out, Address__operation[1]);
  not not_3 (not_3_out, Address__operation[2]);
  not not_4 (not_4_out, Address__operation[3]);
  and and_1 (out_3[0], Data_In, not_1_out, not_2_out, not_3_out, not_4_out);
  and and_2 (out_3[1], Data_In, Address__operation[0], not_2_out, not_3_out, not_4_out);
  and and_3 (out_3[2], Data_In, not_1_out, Address__operation[1], not_3_out, not_4_out);
  and and_4 (out_3[3], Data_In, Address__operation[0], Address__operation[1], not_3_out, not_4_out);
  and and_5 (out_3[4], Data_In, not_1_out, not_2_out, Address__operation[2], not_4_out);
  and and_6 (out_3[5], Data_In, Address__operation[0], not_2_out, Address__operation[2], not_4_out);
  and and_7 (out_3[6], Data_In, not_1_out, Address__operation[1], Address__operation[2], not_4_out);
  and and_8 (out_3[7], Data_In, Address__operation[0], Address__operation[1], Address__operation[2], not_4_out);
  and and_9 (out_3[8], Data_In, not_1_out, not_2_out, not_3_out, Address__operation[3]);
  and and_10 (out_3[9], Data_In, Address__operation[0], not_2_out, not_3_out, Address__operation[3]);
  and and_11 (out_3[10], Data_In, not_1_out, Address__operation[1], not_3_out, Address__operation[3]);
  and and_12 (out_3[11], Data_In, Address__operation[0], Address__operation[1], not_3_out, Address__operation[3]);
  and and_13 (out_3[12], Data_In, not_1_out, not_2_out, Address__operation[2], Address__operation[3]);
  and and_14 (out_3[13], Data_In, Address__operation[0], not_2_out, Address__operation[2], Address__operation[3]);
  and and_15 (out_3[14], Data_In, not_1_out, Address__operation[1], Address__operation[2], Address__operation[3]);
  and and_16 (out_3[15], Data_In, Address__operation[0], Address__operation[1], Address__operation[2], Address__operation[3]);
endmodule

// 4-Bit\nLeft Shift
module _4_bit_left_shift (
  input  [3:0] Input,
  output [3:0] Output
);

  wire and_1_out, and_2_out, and_3_out, and_4_out, and_5_out, and_6_out, and_7_out, and_8_out, and_9_out,
       and_10_out, and_11_out, and_12_out, not_1_out, not_2_out, not_3_out, not_4_out, not_5_out, not_6_out,
       not_7_out, not_8_out;

  and and_1 (and_1_out, 1'b0, 1'b0);
  not not_1 (not_1_out, 1'b0);
  and and_2 (and_2_out, Input[3], not_1_out, not_2_out);
  or or_1 (Output[3], and_1_out, and_2_out, and_3_out);
  not not_2 (not_2_out, 1'b1);
  and and_3 (and_3_out, 1'b1, Input[2]);
  and and_4 (and_4_out, 1'b0, Input[3]);
  not not_3 (not_3_out, 1'b0);
  and and_5 (and_5_out, Input[2], not_3_out, not_4_out);
  or or_2 (Output[2], and_4_out, and_5_out, and_6_out);
  not not_4 (not_4_out, 1'b1);
  and and_6 (and_6_out, 1'b1, Input[1]);
  and and_7 (and_7_out, 1'b0, Input[2]);
  not not_5 (not_5_out, 1'b0);
  and and_8 (and_8_out, Input[1], not_5_out, not_6_out);
  or or_3 (Output[1], and_7_out, and_8_out, and_9_out);
  not not_6 (not_6_out, 1'b1);
  and and_9 (and_9_out, 1'b1, Input[0]);
  and and_10 (and_10_out, 1'b0, Input[1]);
  not not_7 (not_7_out, 1'b0);
  and and_11 (and_11_out, Input[0], not_7_out, not_8_out);
  or or_4 (Output[0], and_10_out, and_11_out, and_12_out);
  not not_8 (not_8_out, 1'b1);
  and and_12 (and_12_out, 1'b1, 1'b0);

  // Notes on the sheet:
  //   Right Shift
  //   Left Shift
endmodule

// 4-Bit\nRight Shift
module _4_bit_right_shift (
  input  [3:0] Input,
  output [3:0] Output
);

  wire and_1_out, and_2_out, and_3_out, and_4_out, and_5_out, and_6_out, and_7_out, and_8_out, and_9_out,
       and_10_out, and_11_out, and_12_out, not_1_out, not_2_out, not_3_out, not_4_out, not_5_out, not_6_out,
       not_7_out, not_8_out;

  and and_1 (and_1_out, 1'b1, 1'b0);
  not not_1 (not_1_out, 1'b1);
  and and_2 (and_2_out, Input[3], not_1_out, not_2_out);
  or or_1 (Output[3], and_1_out, and_2_out, and_3_out);
  not not_2 (not_2_out, 1'b0);
  and and_3 (and_3_out, 1'b0, Input[2]);
  and and_4 (and_4_out, 1'b1, Input[3]);
  not not_3 (not_3_out, 1'b1);
  and and_5 (and_5_out, Input[2], not_3_out, not_4_out);
  or or_2 (Output[2], and_4_out, and_5_out, and_6_out);
  not not_4 (not_4_out, 1'b0);
  and and_6 (and_6_out, 1'b0, Input[1]);
  and and_7 (and_7_out, 1'b1, Input[2]);
  not not_5 (not_5_out, 1'b1);
  and and_8 (and_8_out, Input[1], not_5_out, not_6_out);
  or or_3 (Output[1], and_7_out, and_8_out, and_9_out);
  not not_6 (not_6_out, 1'b0);
  and and_9 (and_9_out, 1'b0, Input[0]);
  and and_10 (and_10_out, 1'b1, Input[1]);
  not not_7 (not_7_out, 1'b1);
  and and_11 (and_11_out, Input[0], not_7_out, not_8_out);
  or or_4 (Output[0], and_10_out, and_11_out, and_12_out);
  not not_8 (not_8_out, 1'b0);
  and and_12 (and_12_out, 1'b0, 1'b0);

  // Notes on the sheet:
  //   Right Shift
  //   Left Shift
endmodule

// 4-Bit Left\nRotate
module _4_bit_left_rotate (
  input  [3:0] Input,
  output [3:0] Output
);

  wire and_1_out, and_2_out, and_3_out, and_4_out, and_5_out, and_6_out, and_7_out, and_8_out, and_9_out,
       and_10_out, and_11_out, and_12_out, not_1_out, not_2_out, not_3_out, not_4_out, not_5_out, not_6_out,
       not_7_out, not_8_out, or_5_out;

  or or_1 (Output[0], Input[3], or_5_out);
  and and_1 (and_1_out, 1'b0, 1'b0);
  not not_1 (not_1_out, 1'b0);
  and and_2 (and_2_out, Input[3], not_1_out, not_2_out);
  or or_2 (Output[3], and_1_out, and_2_out, and_3_out);
  not not_2 (not_2_out, 1'b1);
  and and_3 (and_3_out, 1'b1, Input[2]);
  and and_4 (and_4_out, 1'b0, Input[3]);
  not not_3 (not_3_out, 1'b0);
  and and_5 (and_5_out, Input[2], not_3_out, not_4_out);
  or or_3 (Output[2], and_4_out, and_5_out, and_6_out);
  not not_4 (not_4_out, 1'b1);
  and and_6 (and_6_out, 1'b1, Input[1]);
  and and_7 (and_7_out, 1'b0, Input[2]);
  not not_5 (not_5_out, 1'b0);
  and and_8 (and_8_out, Input[1], not_5_out, not_6_out);
  or or_4 (Output[1], and_7_out, and_8_out, and_9_out);
  not not_6 (not_6_out, 1'b1);
  and and_9 (and_9_out, 1'b1, Input[0]);
  and and_10 (and_10_out, 1'b0, Input[1]);
  not not_7 (not_7_out, 1'b0);
  and and_11 (and_11_out, Input[0], not_7_out, not_8_out);
  or or_5 (or_5_out, and_10_out, and_11_out, and_12_out);
  not not_8 (not_8_out, 1'b1);
  and and_12 (and_12_out, 1'b1, 1'b0);

  // Notes on the sheet:
  //   Right Shift
  //   Left Shift
endmodule

// 4-Bit Right\nRotate
module _4_bit_right_rotate (
  input  [3:0] Input,
  output [3:0] Output
);

  wire and_1_out, and_2_out, and_3_out, and_4_out, and_5_out, and_6_out, and_7_out, and_8_out, and_9_out,
       and_10_out, and_11_out, and_12_out, not_1_out, not_2_out, not_3_out, not_4_out, not_5_out, not_6_out,
       not_7_out, not_8_out, or_1_out;

  and and_1 (and_1_out, 1'b1, 1'b0);
  not not_1 (not_1_out, 1'b1);
  and and_2 (and_2_out, Input[3], not_1_out, not_2_out);
  or or_1 (or_1_out, and_1_out, and_2_out, and_3_out);
  not not_2 (not_2_out, 1'b0);
  and and_3 (and_3_out, 1'b0, Input[2]);
  and and_4 (and_4_out, 1'b1, Input[3]);
  not not_3 (not_3_out, 1'b1);
  and and_5 (and_5_out, Input[2], not_3_out, not_4_out);
  or or_2 (Output[2], and_4_out, and_5_out, and_6_out);
  not not_4 (not_4_out, 1'b0);
  and and_6 (and_6_out, 1'b0, Input[1]);
  and and_7 (and_7_out, 1'b1, Input[2]);
  not not_5 (not_5_out, 1'b1);
  and and_8 (and_8_out, Input[1], not_5_out, not_6_out);
  or or_3 (Output[1], and_7_out, and_8_out, and_9_out);
  not not_6 (not_6_out, 1'b0);
  and and_9 (and_9_out, 1'b0, Input[0]);
  and and_10 (and_10_out, 1'b1, Input[1]);
  not not_7 (not_7_out, 1'b1);
  and and_11 (and_11_out, Input[0], not_7_out, not_8_out);
  or or_4 (Output[0], and_10_out, and_11_out, and_12_out);
  not not_8 (not_8_out, 1'b0);
  and and_12 (and_12_out, 1'b0, 1'b0);
  or or_5 (Output[3], or_1_out, Input[0]);

  // Notes on the sheet:
  //   Right Shift
  //   Left Shift
endmodule

// 16-to-4 Multiplexer
module _16_to_4_multiplexer (
  input  [3:0] Data,
  input  [3:0] Data_2,
  input  [3:0] Data_3,
  input  [3:0] Data_4,
  input  [3:0] Data_5,
  input  [3:0] Data_6,
  input  [3:0] Data_7,
  input  [3:0] Data_8,
  input  [3:0] Data_9,
  input  [3:0] Data_10,
  input  [3:0] Data_11,
  input  [3:0] Data_12,
  input  [3:0] Data_13,
  input  [3:0] Data_14,
  input  [3:0] Data_15,
  input  [3:0] Data_16,
  input  [3:0] Operation,
  output [3:0] Operation_2
);

  wire not_1_out, not_2_out, not_3_out, not_4_out;
  wire [3:0] n4_bit_and_1_output, n4_bit_and_2_output, n4_bit_and_3_output, n4_bit_and_4_output,
       n4_bit_and_5_output, n4_bit_and_6_output, n4_bit_and_7_output, n4_bit_and_8_output,
       n4_bit_and_9_output, n4_bit_and_10_output, n4_bit_and_11_output, n4_bit_and_12_output,
       n4_bit_and_13_output, n4_bit_and_14_output, n4_bit_and_15_output, n4_bit_and_16_output,
       n4_bit_or_1_output, n4_bit_or_2_output, n4_bit_or_3_output, n4_bit_or_4_output, n4_bit_or_5_output,
       n4_bit_or_6_output, n4_bit_or_7_output, n4_bit_or_9_output, n4_bit_or_10_output, n4_bit_or_11_output,
       n4_bit_or_12_output, n4_bit_or_13_output, n4_bit_or_14_output, n4_bit_or_15_output, undriven;
  wire [3:3] and_1_out, and_2_out, and_3_out, and_4_out, and_5_out, and_6_out, and_7_out, and_8_out,
       and_9_out, and_10_out, and_11_out, and_12_out, and_13_out, and_14_out, and_15_out, and_16_out;

  not not_1 (not_1_out, Operation[0]);
  not not_2 (not_2_out, Operation[1]);
  not not_3 (not_3_out, Operation[2]);
  not not_4 (not_4_out, Operation[3]);
  and and_1 (and_1_out[3], Operation[3], Operation[2], Operation[1], Operation[0]);
  _4_bit_and u_4_bit_and_1 (.A_In({4{and_1_out[3]}}), .B_In(Data), .Output(n4_bit_and_1_output));
  and and_2 (and_2_out[3], Operation[3], Operation[2], Operation[1], not_1_out);
  _4_bit_and u_4_bit_and_2 (.A_In({4{and_2_out[3]}}), .B_In(Data_2), .Output(n4_bit_and_2_output));
  _4_bit_or u_4_bit_or_1 (.A_In(n4_bit_and_1_output), .B_In(n4_bit_and_2_output), .Output(n4_bit_or_1_output));
  _4_bit_or u_4_bit_or_2 (.A_In(n4_bit_or_1_output), .B_In(n4_bit_or_3_output), .Output(n4_bit_or_2_output));
  and and_3 (and_3_out[3], Operation[3], Operation[2], not_2_out, Operation[0]);
  _4_bit_and u_4_bit_and_3 (.A_In({4{and_3_out[3]}}), .B_In(Data_3), .Output(n4_bit_and_3_output));
  _4_bit_or u_4_bit_or_3 (.A_In(n4_bit_and_3_output), .B_In(n4_bit_and_4_output), .Output(n4_bit_or_3_output));
  and and_4 (and_4_out[3], Operation[3], Operation[2], not_2_out, not_1_out);
  _4_bit_and u_4_bit_and_4 (.A_In({4{and_4_out[3]}}), .B_In(Data_4), .Output(n4_bit_and_4_output));
  and and_5 (and_5_out[3], Operation[3], not_3_out, Operation[1], Operation[0]);
  _4_bit_or u_4_bit_or_4 (.A_In(n4_bit_or_2_output), .B_In(n4_bit_or_6_output), .Output(n4_bit_or_4_output));
  _4_bit_and u_4_bit_and_5 (.A_In({4{and_5_out[3]}}), .B_In(Data_5), .Output(n4_bit_and_5_output));
  _4_bit_or u_4_bit_or_5 (.A_In(n4_bit_and_5_output), .B_In(n4_bit_and_6_output), .Output(n4_bit_or_5_output));
  and and_6 (and_6_out[3], Operation[3], not_3_out, Operation[1], not_1_out);
  _4_bit_and u_4_bit_and_6 (.A_In({4{and_6_out[3]}}), .B_In(Data_6), .Output(n4_bit_and_6_output));
  _4_bit_or u_4_bit_or_6 (.A_In(n4_bit_or_5_output), .B_In(n4_bit_or_7_output), .Output(n4_bit_or_6_output));
  and and_7 (and_7_out[3], Operation[3], not_3_out, not_2_out, Operation[0]);
  _4_bit_and u_4_bit_and_7 (.A_In({4{and_7_out[3]}}), .B_In(undriven), .Output(n4_bit_and_7_output));
  and and_8 (and_8_out[3], Operation[3], not_3_out, not_2_out, not_1_out);
  _4_bit_or u_4_bit_or_7 (.A_In(n4_bit_and_7_output), .B_In(n4_bit_and_8_output), .Output(n4_bit_or_7_output));
  _4_bit_and u_4_bit_and_8 (.A_In({4{and_8_out[3]}}), .B_In(Data_8), .Output(n4_bit_and_8_output));
  _4_bit_or u_4_bit_or_8 (.A_In(n4_bit_or_4_output), .B_In(n4_bit_or_12_output), .Output(Operation_2));
  and and_9 (and_9_out[3], not_4_out, Operation[2], Operation[1], Operation[0]);
  _4_bit_and u_4_bit_and_9 (.A_In({4{and_9_out[3]}}), .B_In(Data_9), .Output(n4_bit_and_9_output));
  _4_bit_or u_4_bit_or_9 (.A_In(n4_bit_and_9_output), .B_In(n4_bit_and_10_output), .Output(n4_bit_or_9_output));
  and and_10 (and_10_out[3], not_4_out, Operation[2], Operation[1], not_1_out);
  _4_bit_and u_4_bit_and_10 (.A_In({4{and_10_out[3]}}), .B_In(Data_10), .Output(n4_bit_and_10_output));
  and and_11 (and_11_out[3], not_4_out, Operation[2], not_2_out, Operation[0]);
  _4_bit_or u_4_bit_or_10 (.A_In(n4_bit_or_9_output), .B_In(n4_bit_or_11_output), .Output(n4_bit_or_10_output));
  _4_bit_and u_4_bit_and_11 (.A_In({4{and_11_out[3]}}), .B_In(Data_11), .Output(n4_bit_and_11_output));
  _4_bit_or u_4_bit_or_11 (.A_In(n4_bit_and_11_output), .B_In(n4_bit_and_12_output), .Output(n4_bit_or_11_output));
  and and_12 (and_12_out[3], not_4_out, Operation[2], not_2_out, not_1_out);
  _4_bit_and u_4_bit_and_12 (.A_In({4{and_12_out[3]}}), .B_In(Data_12), .Output(n4_bit_and_12_output));
  _4_bit_or u_4_bit_or_12 (.A_In(n4_bit_or_10_output), .B_In(n4_bit_or_14_output), .Output(n4_bit_or_12_output));
  and and_13 (and_13_out[3], not_4_out, not_3_out, Operation[1], Operation[0]);
  _4_bit_and u_4_bit_and_13 (.A_In({4{and_13_out[3]}}), .B_In(Data_13), .Output(n4_bit_and_13_output));
  _4_bit_or u_4_bit_or_13 (.A_In(n4_bit_and_13_output), .B_In(n4_bit_and_14_output), .Output(n4_bit_or_13_output));
  and and_14 (and_14_out[3], not_4_out, not_3_out, Operation[1], not_1_out);
  _4_bit_and u_4_bit_and_14 (.A_In({4{and_14_out[3]}}), .B_In(Data_14), .Output(n4_bit_and_14_output));
  _4_bit_or u_4_bit_or_14 (.A_In(n4_bit_or_13_output), .B_In(n4_bit_or_15_output), .Output(n4_bit_or_14_output));
  and and_15 (and_15_out[3], not_4_out, not_3_out, not_2_out, Operation[0]);
  _4_bit_and u_4_bit_and_15 (.A_In({4{and_15_out[3]}}), .B_In(Data_15), .Output(n4_bit_and_15_output));
  _4_bit_or u_4_bit_or_15 (.A_In(n4_bit_and_15_output), .B_In(n4_bit_and_16_output), .Output(n4_bit_or_15_output));
  and and_16 (and_16_out[3], not_4_out, not_3_out, not_2_out, not_1_out);
  _4_bit_and u_4_bit_and_16 (.A_In({4{and_16_out[3]}}), .B_In(Data_16), .Output(n4_bit_and_16_output));
endmodule

// 4-to-2\nMultiplexer
module _4_to_for_multiplexer (
  input  Data,
  input  Data_2,
  input  Data_3,
  input  Data_4,
  input  [3:0] Operation,
  output Operation_2
);

  wire and_1_out, and_2_out, and_3_out, and_4_out, not_1_out, not_2_out;

  not not_1 (not_1_out, Operation[0]);
  not not_2 (not_2_out, Operation[1]);
  and and_1 (and_1_out, Operation[1], Operation[0], Data);
  and and_2 (and_2_out, Operation[1], not_1_out, Data_2);
  or or_1 (Operation_2, and_1_out, and_2_out, and_3_out, and_4_out);
  and and_3 (and_3_out, not_2_out, Operation[0], Data_3);
  and and_4 (and_4_out, not_2_out, not_1_out, Data_4);
endmodule

module print (
  input  Load,
  input  [3:0] A_Input,
  input  [3:0] B_Input,
  input  On,
  input  [3:0] Operation,
  output Maximum_Count_Reached,
  output [3:0] Output,
  output C,
  output N,
  output Z,
  output V
);

  wire and_1_out, and_2_out, and_3_out, Clock_out, d_ff_1_q, n4_bit_decrementer_1_carry_out,
       n4_bit_full_adder_1_carry_out, n4_bit_increment_1_carry_out, n4_bit_subtractor_1_overflow___underflow,
       not_1_out, not_2_out, not_3_out, not_4_out, or_1_out, or_3_out, t_ff_1_q, xor_1_out;
  wire [3:0] A_q, B_q, controlled_buffer_1_out, n4_bit_and_1_output, n4_bit_decrementer_1_output,
       n4_bit_full_adder_1_output, n4_bit_increment_1_output, n4_bit_left_rotate_1_output,
       n4_bit_left_shift_1_output, n4_bit_or_1_output, n4_bit_right_rotate_1_output,
       n4_bit_right_shift_1_output, n4_bit_subtractor_1_output, n4_bit_xor_1_output, register_1_q;

  Clock Clock (.out(Clock_out));
  and and_1 (and_1_out, Clock_out, t_ff_1_q);
  Counter #(.width(4), .max('h3)) counter_1 (
    .carry(Maximum_Count_Reached), .clk(and_1_out), .clr(d_ff_1_q));  // open: load, D, count, Q
  T_Flip_Flop t_ff_1 (
    .clk(Clock_out), .T(1'b1), .Q(t_ff_1_q), .reset(Maximum_Count_Reached), .en(On));  // open: Qn, preset
  assign controlled_buffer_1_out = Load ? A_Input : 4'bz;  // Controlled_Buffer controlled_buffer_1
  D_Flip_Flop d_ff_1 (.clk(Clock_out), .D(Maximum_Count_Reached), .Q(d_ff_1_q), .en(1'b1));  // open: Qn, preset, reset
  or or_1 (or_1_out, Load, Maximum_Count_Reached);
  assign controlled_buffer_1_out = not_1_out ? register_1_q : 4'bz;  // Controlled_Buffer controlled_buffer_2
  not not_1 (not_1_out, Load);
  Register #(.width(4)) A (.D(controlled_buffer_1_out), .en(or_1_out), .Q(A_q), .clk(Clock_out));  // open: clr
  Register #(.width(4)) B (.D(B_Input), .Q(B_q), .clk(Clock_out));  // open: en, clr
  _4_bit_xor u_4_bit_xor_1 (.A_In(A_q), .B_In(B_q), .Output(n4_bit_xor_1_output));
  _4_bit_or u_4_bit_or_1 (.A_In(A_q), .B_In(B_q), .Output(n4_bit_or_1_output));
  _4_bit_and u_4_bit_and_1 (.A_In(A_q), .B_In(B_q), .Output(n4_bit_and_1_output));
  _4_bit_right_rotate u_4_bit_right_rotate_1 (.Input(A_q), .Output(n4_bit_right_rotate_1_output));
  _4_bit_left_rotate u_4_bit_left_rotate_1 (.Input(A_q), .Output(n4_bit_left_rotate_1_output));
  _16_to_4_multiplexer u_16_to_4_multiplexer_1 (
    .Operation(Operation), .Operation_2({N, Output[2:0]}), .Data_16(n4_bit_full_adder_1_output),
    .Data_15(n4_bit_subtractor_1_output), .Data_14(n4_bit_increment_1_output),
    .Data_13(n4_bit_decrementer_1_output), .Data_9(n4_bit_right_rotate_1_output),
    .Data_10(n4_bit_left_rotate_1_output), .Data_11(n4_bit_right_shift_1_output),
    .Data_12(n4_bit_left_shift_1_output), .Data_6(n4_bit_xor_1_output), .Data_7(n4_bit_or_1_output),
    .Data_8(n4_bit_and_1_output));  // open: Data_5, Data, Data_2, Data_3, Data_4
  _4_bit_right_shift u_4_bit_right_shift_1 (.Input(A_q), .Output(n4_bit_right_shift_1_output));
  _4_bit_left_shift u_4_bit_left_shift_1 (.Input(A_q), .Output(n4_bit_left_shift_1_output));
  Register #(.width(4)) register_1 (.D({N, Output[2:0]}), .Q(register_1_q), .clk(Clock_out));  // open: en, clr
  _4_bit_decrementer u_4_bit_decrementer_1 (
    .Input(A_q), .Output(n4_bit_decrementer_1_output), .Carry_Out(n4_bit_decrementer_1_carry_out));
  _4_bit_increment u_4_bit_increment_1 (
    .Input(A_q), .Carry_Out(n4_bit_increment_1_carry_out), .Output(n4_bit_increment_1_output));
  _4_to_for_multiplexer u_4_to_for_multiplexer_1 (
    .Operation(Operation), .Data(n4_bit_decrementer_1_carry_out), .Data_2(n4_bit_increment_1_carry_out),
    .Data_3(n4_bit_subtractor_1_overflow___underflow), .Data_4(n4_bit_full_adder_1_carry_out), .Operation_2(C));
  xor xor_1 (xor_1_out, A_q[3], 1'b0);
  and and_2 (and_2_out, xor_1_out, A_q[3], not_2_out);
  _4_bit_subtractor u_4_bit_subtractor_1 (
    .B_In(B_q), .A_In(A_q), .Output(n4_bit_subtractor_1_output),
    .Overflow___Underflow(n4_bit_subtractor_1_overflow___underflow), .in_3(1'b1));
  not not_2 (not_2_out, N);
  not not_3 (not_3_out, xor_1_out);
  or or_2 (V, and_2_out, and_3_out);
  not not_4 (not_4_out, A_q[3]);
  and and_3 (and_3_out, not_3_out, not_4_out, N);
  _4_bit_full_adder u_4_bit_full_adder_1 (
    .A_In(A_q), .B_In(B_q), .Output(n4_bit_full_adder_1_output), .Carry_Out(n4_bit_full_adder_1_carry_out),
    .Carry_In(1'b0));
  or or_3 (or_3_out, N, Output[2], Output[1], Output[0]);
  not not_5 (Z, or_3_out);

  assign Output[3] = N;
endmodule
